// Digital circuit ALU-HACK.dig as structural Verilog
module ALU_HACK (
  input  [15:0] X,
  input  [6:0] ALU_OP,
  input  [15:0] Y,
  output [15:0] OUT,
  output ng,
  output zr
);

  wire [15:0] add_1_s, and_1_out, multiplexer_1_out, multiplexer_2_out, multiplexer_3_out, multiplexer_4_out,
       multiplexer_5_out, not_1_out, not_2_out, not_3_out;

  Multiplexer #(.Bits(16)) multiplexer_1 (.sel(ALU_OP[0]), .in_0(X), .in_1({16{1'b0}}), .out(multiplexer_1_out));
  Multiplexer #(.Bits(16)) multiplexer_2 (.sel(ALU_OP[2]), .in_0(Y), .in_1({16{1'b0}}), .out(multiplexer_2_out));
  assign not_1_out = ~multiplexer_1_out;  // Not not_1, 16 bits wide
  assign not_2_out = ~multiplexer_2_out;  // Not not_2, 16 bits wide
  Multiplexer #(.Bits(16)) multiplexer_3 (
    .sel(ALU_OP[1]), .in_0(multiplexer_1_out), .in_1(not_1_out), .out(multiplexer_3_out));
  Multiplexer #(.Bits(16)) multiplexer_4 (
    .sel(ALU_OP[3]), .in_0(multiplexer_2_out), .in_1(not_2_out), .out(multiplexer_4_out));
  assign and_1_out = multiplexer_3_out & multiplexer_4_out;  // And and_1, 16 bits wide
  Add #(.Bits(16)) add_1 (.a(multiplexer_3_out), .b(multiplexer_4_out), .c_i(ALU_OP[4]), .s(add_1_s));  // open: c_o
  Multiplexer #(.Bits(16)) multiplexer_5 (.sel(ALU_OP[5]), .in_0(and_1_out), .in_1(add_1_s), .out(multiplexer_5_out));
  assign not_3_out = ~multiplexer_5_out;  // Not not_3, 16 bits wide
  Multiplexer #(.Bits(16)) multiplexer_6 (
    .sel(ALU_OP[6]), .in_0(multiplexer_5_out), .in_1(not_3_out), .out({ng, OUT[14:0]}));
  nor nor_1 (zr, OUT[0], OUT[1], OUT[2], OUT[3], OUT[4], OUT[5], OUT[6], OUT[7], OUT[9], OUT[10], OUT[11], OUT[12], OUT[13], OUT[14], OUT[8], ng);

  assign OUT[15] = ng;

  // Notes on the sheet:
  //   BIT | DESC
  //   0 | zx
  //   1 | nx
  //   2 | zy
  //   3 | ny
  //   4 | inc
  //   5 | f
  //   6 | no
endmodule
